// Logisim project TinyCPU.circ as structural Verilog: 5 circuits, main circuit TinyCPU
module TinyCPU (
);

  Datapath datapath_1 ();  // open: DATA_IN, ACC_LOAD, VALID_IN, CLK, ACC_OUT, ACC_VALID_OUT, ZERO, NEGATIVE
  AddressPath addresspath_1 ();  // open: ADDRESS_IN, OFFSET, AR_LOAD, VALID_IN, CLK, ADDRESS, ADDRESS_VALID, ADDRESS_PLUS_OFFSET, OFFSET_CARRY
  Memory memory_1 ();
  ErrorFlags errorflags_1 ();

  // Notes on the sheet:
  //   TinyCPU 16/12 starter — wire and verify each subcircuit before adding control logic
endmodule

module Datapath (
  input  [15:0] DATA_IN,
  input  ACC_LOAD,
  input  VALID_IN,
  input  CLK,
  output [15:0] ACC_OUT,
  output ACC_VALID_OUT,
  output ZERO,
  output NEGATIVE
);

  wire undriven;

  Register #(.width(16)) ACC (.D(DATA_IN), .Q(ACC_OUT), .clk(undriven));  // open: en, clr
  Register #(.width(1)) ACC_VALID (.D(VALID_IN), .Q(ACC_VALID_OUT), .clk(undriven));  // open: en, clr
  Comparator #(.mode("twosComplement"), .width(16)) ACC_STATUS (
    .a(ACC_OUT), .b({16{1'b0}}), .eq(ZERO), .lt(NEGATIVE));  // open: gt

  // Notes on the sheet:
  //   Clocked 16-bit accumulator; signed comparator derives ZERO and NEGATIVE
endmodule

module AddressPath (
  input  [11:0] ADDRESS_IN,
  input  [11:0] OFFSET,
  input  AR_LOAD,
  input  VALID_IN,
  input  CLK,
  output [11:0] ADDRESS,
  output ADDRESS_VALID,
  output [11:0] ADDRESS_PLUS_OFFSET,
  output OFFSET_CARRY
);

  Register #(.width(12)) AR (.D(ADDRESS_IN), .Q(ADDRESS), .clk(AR_LOAD));  // open: en, clr
  Register #(.width(1)) AR_VALID (.D(VALID_IN), .Q(ADDRESS_VALID), .clk(AR_LOAD));  // open: en, clr
  // Adder #(.width(12)) OFFSET_ADDER: pin names not known; wires that end beside it: ADDRESS, OFFSET, ADDRESS_PLUS_OFFSET, OFFSET_CARRY

  // Notes on the sheet:
  //   Clocked 12-bit address register with combinational offset addition
endmodule

module Memory (
);

  RAM #(.addrWidth(12), .dataWidth(16)) DATA_RAM ();  // open: addr, we, oe, clk, din, dout
  RAM #(.addrWidth(12), .dataWidth(1)) VALID_RAM ();  // open: addr, we, oe, clk, din, dout

  // Notes on the sheet:
  //   Parallel value/valid RAM — shared address and write-enable are the next wiring step
endmodule

module ErrorFlags (
);

  Register #(.width(1)) OVF ();  // open: D, en, clk, Q, clr
  Register #(.width(1)) INV ();  // open: D, en, clk, Q, clr
  Register #(.width(1)) DIV0 ();  // open: D, en, clk, Q, clr
  Register #(.width(1)) ILL ();  // open: D, en, clk, Q, clr
  Register #(.width(1)) ADDR ();  // open: D, en, clk, Q, clr
  Register #(.width(1)) INPUT ();  // open: D, en, clk, Q, clr

  // Notes on the sheet:
  //   Sticky set-dominant error state; CLEAR_ERROR must be the sole clear source
endmodule
