// Logisim project TinyCPU-FetchDecode.circ as structural Verilog: 1 circuit, main circuit FetchDecode
module FetchDecode (
  input  CLK,
  input  RESET,
  input  DEC_JUMP_NOT_ZERO,
  input  NOT_ZERO,
  input  [15:0] PROGRAM_LIMIT,
  input  DEC_HALT_ERROR,
  output JUMP_NOT_ZERO,
  output HALT_ERROR,
  output [11:0] PC_OUT,
  output [21:0] OPCODE
);

  wire PROGRAM_LIMIT_COMPARE_gt;
  wire [15:0] adder_1_out, PC_NEXT_SELECT_out;
  wire [15:12] PC_q;

  Register #(.width(16)) PC (.D(PC_NEXT_SELECT_out), .en(1'b1), .clk(CLK), .Q({PC_q, PC_OUT}), .clr(RESET));
  and JNZ_TAKEN (JUMP_NOT_ZERO, DEC_JUMP_NOT_ZERO, NOT_ZERO);
  Adder #(.width(16)) adder_1 (.a({PC_q, PC_OUT}), .b(16'h1), .out(adder_1_out));  // open: cin, cout
  Comparator #(.width(16)) PROGRAM_LIMIT_COMPARE (
    .a({PC_q, PC_OUT}), .b(PROGRAM_LIMIT), .gt(PROGRAM_LIMIT_COMPARE_gt));  // open: eq, lt
  ROM #(.addrWidth(12), .dataWidth(22)) INSTRUCTION_ROM (.addr(PC_OUT), .data(OPCODE));
  Multiplexer #(.width(16)) PC_NEXT_SELECT (
    .in0(adder_1_out), .in1(OPCODE[15:0]), .out(PC_NEXT_SELECT_out), .sel(JUMP_NOT_ZERO));
  or ERROR_HALT (HALT_ERROR, PROGRAM_LIMIT_COMPARE_gt, DEC_HALT_ERROR);

  // Notes on the sheet:
  //   PROGRAM_LIMIT: initial=0xfff
  //   AP 7 machine format v1: stable six-bit opcode allocation and encoder-generated ROM
  //   contents of INSTRUCTION_ROM (hex, n*v repeats v):
  //   00ffff 1c0065 000003 1c0064 2a0000 04ffff 1c0064 240004 2c0000
endmodule
